# Fritzing sketch scotts_hbridge (saved by Fritzing 0.9.3b)
circuit board: 5.1cm x 4.45cm
breadboards: 1

parts:
  U1 = Optocoupler [package=THT]
  U2 = Optocoupler [package=THT]
  Q5 = Basic FET N-Channel [package="TO220 [THT]"]
  Q6 = Basic FET P-Channel [package="TO220 [THT]"]
  Q7 = Basic FET N-Channel [package="TO220 [THT]"]
  Q8 = Basic FET P-Channel [package="TO220 [THT]"]
  J1 = Camdenboss CTB0158-4 [part_number=CTB0158-4 package=THT]
  J2 = Camdenboss CTB0158-2 [part_number=CTB0158-2 package=THT]
  R4 = Resistor [tolerance=±5% resistance=10k package=THT]
  R2 = Resistor [tolerance=±5% resistance=1k package=THT]
  R3 = Resistor [tolerance=±5% resistance=10k package=THT]
  R5 = Resistor [tolerance=±5% resistance=1k package=THT]

nets:
  N1: U1.Pin_1, R2.Pin_0
  GND: U1.Pin_2, U1.Pin_4, U2.Pin_2, U2.Pin_4, Q5.source, Q7.source, J1.pin4
  N2: U1.Pin_5, Q5.gate, Q8.gate, R4.Pin_0
  N3: U2.Pin_1, R5.Pin_0
  N4: U2.Pin_5, Q6.gate, Q7.gate, R3.Pin_0
  N5: Q5.drain, Q8.drain, J1.pin2
  N6: Q6.drain, Q7.drain, J1.pin3
  12V: Q6.source, Q8.source, J1.pin1, R4.Pin_1, R3.Pin_1
  N7: J2.pin1, R2.Pin_1
  N8: J2.pin2, R5.Pin_1

notes:
  Vcc
  Motor 1
  Motor 2
  GND
  A
  B
